# Fritzing sketch tamiyahacktank (saved by Fritzing 0.9.3b)
breadboards: 1

parts:
  パーツ1 = Arduino Uno (Rev3)
  U1 = TA7291P [package=HSIP10-P-2.54(THT)]
  U2 = TA7291P [package=HSIP10-P-2.54(THT)]
  M1 = DC Motor
  M2 = DC Motor
  VCC1 = Battery
  パーツ2 = SRF05 Ultrasonic Rangefinder  # not connected

nets (from the schematic view):
  GND: パーツ1.GND, U1.GND, U2.GND, VCC1.-
  N1: パーツ1.D2, U1.IN1
  N2: パーツ1.D3_PWM, U1.IN2
  N3: パーツ1.D4, U2.IN1
  N4: パーツ1.D5_PWM, U2.IN2
  VCC: パーツ1.5V, U1.Vcc, U2.Vcc
  N5: U1.OUT1, M1.pin_2
  N6: U1.Vref, U1.Vs, U2.Vref, U2.Vs, VCC1.+
  N7: U1.OUT2, M1.pin_1
  N8: U2.OUT1, M2.pin_2
  N9: U2.OUT2, M2.pin_1

custom parts:
  TA7291P: The IC are Full-Bridge Driver. 4 modes available (CW / CCW / STOP / BRAKE) and PWM control. Output current:1.0 A (AVE.) 2.0 A (PEAK)
